# Fritzing sketch sdfatlib-stm32f103c8con (saved by Fritzing 0.9.4)

parts:
  M1 = STM32F103C8T6 blue mini board
  microSD_Transflash1 = SparkFun - microSD Transflash
  SparkFun_Serial_Basic_Breakout_-_CH340G1 = SparkFun Serial Basic Breakout - CH340G [part_number=DEV-14050]  # not connected

nets:
  N1: M1.B13, microSD_Transflash1.SCK
  N2: M1.B14, microSD_Transflash1.DO
  N3: M1.B15, microSD_Transflash1.DI
  N4: M1.A8, microSD_Transflash1.CS
  GND: M1.G, M1.GND, microSD_Transflash1.GND
  3.3V: M1.3.3V, M1.3.3, microSD_Transflash1.VCC

notes:
  CH340G USB to Serial Module
  Micro SD Card Module
  STM32F103C8T6 Development Board

custom parts:
  SparkFun Serial Basic Breakout - CH340G: The SparkFun Serial Basic Breakout is an easy-to-use USB-to-Serial adapter based on the CH340G IC from WCH. It works with 5V and 3.3V systems and should auto install on most operating systems without the need for additional drivers. The Serial Basic uses the CH340G IC to quickly and easily convert serial signals to USB. It’s a great lower-cost alternative to the extremely popular FTDI Basic.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
